# Fritzing sketch LED-Switch (saved by Fritzing 0.9.3b)
circuit board: 8.46667cm x 5.64444cm
breadboards: 1

parts:
  R1 = Resistor [tolerance=±5% resistance=100 package=THT]
  Bauteil1 = SparkFun ESP8266 Thing
  LED1 = smd LED [color="Red (633nm)" package="0603 [SMD]"]
  V1 = DC Power [voltage=5V]

nets:
  N1: R1.Pin_0, Bauteil1.GPIO4
  N2: R1.Pin_1, LED1.cathode
  N3: Bauteil1.GND, LED1.anode, V1.V-
  N4: Bauteil1.VIN, V1.V+
