# Fritzing sketch LED-Switch (saved by Fritzing 0.9.4)
circuit board: 8.46667cm x 5.64444cm
breadboards: 1

parts:
  Bauteil1 = SparkFun ESP8266 Thing
  U1 = RELAY [package=relay-g5q]
  U2 = RELAY [package=relay-g5q]
  V1 = DC Power [voltage=12V]
  M1 = DC Motor
  U3 = LM3480IM4 [package=sot23-3]
  J1 = Screw terminal - 2 pins [package=THT]

nets:
  GND: Bauteil1.GND, U1.COIL2, U1.NC, U2.COIL2, U2.NC, V1.V-, U3.GND, J1.pin1
  N1: Bauteil1.VIN, U3.OUT
  N2: Bauteil1.GPIO5, U1.COIL1
  N3: Bauteil1.GPIO4, U2.COIL1
  N4: U1.MAIN, M1.pin_2
  N5: U1.NO, U2.NO, V1.V+, U3.IN, J1.pin2
  N6: U2.MAIN, M1.pin_1
