# Fritzing sketch LED-Switch (saved by Fritzing 0.9.4)
circuit board: 14.552cm x 7.53354cm
breadboards: 1

parts:
  ESP8266 = SparkFun ESP8266 Thing
  Valve_Motor = DC Motor
  LM1 = Voltage Regulator - 3.3V [package=TO-220-5]
  LM2 = Voltage Regulator - 3.3V [part_number="5V Variant" package=TO-220-5]
  C1 = Capacitor Polarized [part_number=100uF package=panasonic_h13]
  L1 = Inductor [package="400 mil [THT]"]
  D1 = Schottky Diode [part_number=1N5817 package="300 mil [THT]"]
  C3 = Capacitor Polarized [part_number=100uF package=panasonic_h13]
  L2 = Inductor [package="400 mil [THT]"]
  C4 = Electrolytic Capacitor [capacitance=330µF package="100 mil [THT, electrolytic]"]
  D2 = Schottky Diode [part_number=1N5817 package="300 mil [THT]"]
  Relay_1 = KY-019 5V Relay Module [package="Breakout board"]
  Relay_2 = KY-019 5V Relay Module [package="Breakout board"]
  C5 = Electrolytic Capacitor [capacitance=330µF package="100 mil [THT, electrolytic]"]
  J1 = Screw terminal - 2 pins [package=THT]
  S1 = SWITCH-MOMENTARY-2 [package=tactile-pth]
  S2 = SWITCH-MOMENTARY-2 [package=tactile-pth]

nets:
  N1: ESP8266.GPIO14, S1.1
  GND: ESP8266.GND, LM1.GND, LM1.ON/OFF, C3.-, C4.-, D2.anode
  N2: ESP8266.VIN, LM1.Feedback, L2.pin_1, C4.+
  N3: ESP8266.GPIO5, Relay_1.S
  N4: ESP8266.GPIO4, Relay_2.S
  N5: ESP8266.GPIO13, S2.1
  N6: Valve_Motor.pin_1, Relay_2.Common
  N7: Valve_Motor.pin_2, Relay_1.Common
  N8: LM1.+Vin, LM2.+Vin, C1.+, C3.+, Relay_1.NO, Relay_2.NO, J1.pin2
  N9: LM1.+Vout, L2.pin_0, D2.cathode
  N10: LM2.+Vout, L1.pin_0, D1.cathode
  N11: LM2.GND, LM2.ON/OFF, C1.-, D1.anode, Relay_1.-, Relay_1.NC, Relay_2.-, Relay_2.NC, C5.-, J1.pin1, S1.2, S2.2
  N12: LM2.Feedback, L1.pin_1, Relay_1.+, Relay_2.+, C5.+

custom parts:
  Voltage Regulator - 3.3V: 3.3V DC Voltage Regulator LM2575 TO-220-5
  KY-019 5V Relay Module: KY-019 5V Relay module, used to control AC circuits.
